# Fritzing sketch OpenPull (saved by Fritzing 0.9.3b)
breadboards: 1
perfboards: 1

parts:
  Bauteil1 = Arduino Nano (Rev3.0)
  M1 = Stepper Motor - Bipolar
  M2 = Stepper Motor - Bipolar
  Pololu_A1 = Pololu A4988 [package=SO16]
  Pololu_A2 = Pololu A4988 [package=SO16]
  Part1 = HX711 Weighing Sensor Module
  C1 = Electrolytic Capacitor [capacitance=1µF package="100 mil [THT, electrolytic]"]
  Power_plug1 = Power plug
  M3 = Stepper Motor - Bipolar
  S1 = Pushbutton [package="[THT]"]
  S4 = Pushbutton [package="[THT]"]
  S5 = Toggle Switch [package=THT]
  J1 = female pin header, 4 pins [form="♀ (female)"]
  LED1 = LED - 5mm [color="Green (555nm)" package="5 mm [THT]"]
  R1 = Resistor [tolerance=±5% resistance=220 package=THT]

nets:
  N1: Bauteil1.D2, Pololu_A1.STEP, Pololu_A2.STEP
  N2: Bauteil1.D3, Pololu_A1.DIR, Pololu_A2.DIR
  N3: Bauteil1.D4, Bauteil1.D6, Pololu_A1.MS2, Pololu_A1.MS3, Pololu_A1.GND#8, Pololu_A2.MS2, Pololu_A2.MS3, Pololu_A2.GND#8, Part1.GND, S1.Pin_3, S1.Pin_4, S4.Pin_3, S4.Pin_4, S5.COM, J1.pin2, J1.pin4, R1.Pin_0
  N4: Bauteil1.D5, S5.L1, J1.pin1
  N5: Bauteil1.D7, LED1.anode
  N6: Bauteil1.A1, Part1.CK/TX
  N7: Bauteil1.A0, Part1.DO/RX
  N8: M1.A, Pololu_A1.2B
  N9: M1.C, Pololu_A1.2A
  N10: M1.B, Pololu_A1.1A
  N11: M1.D, Pololu_A1.1B
  N12: M2.A, Pololu_A2.2B
  N13: M2.C, Pololu_A2.2A
  N14: M2.B, Pololu_A2.1A
  N15: M2.D, Pololu_A2.1B
  VDD: Pololu_A1.MS1, Pololu_A1.VDD, Pololu_A2.MS1, Pololu_A2.VDD, Part1.VCC
  N16: Pololu_A1.RESET, Pololu_A1.SLEEP
  N17: Pololu_A1.GND#14, Pololu_A2.GND#14, C1.-, Power_plug1.GND
  N18: Pololu_A1.VMOT, Pololu_A2.VMOT, C1.+, Power_plug1.VCC
  N19: Pololu_A2.RESET, Pololu_A2.SLEEP
  N20: Part1.E+, M3.D
  N21: Part1.E-, M3.B
  N22: Part1.A+, M3.C
  N23: Part1.A-, M3.A
  N24: S1.Pin_1, S1.Pin_2
  N25: S4.Pin_1, S4.Pin_2
  N26: LED1.cathode, R1.Pin_1

notes:
  I am the load cell!
